// Logisim project alu_4bits.circ as structural Verilog: 11 circuits, main circuit Main
module Main (
  input  A1,
  input  A2,
  input  A3,
  input  A4,
  input  B1,
  input  B2,
  input  B3,
  input  B4,
  input  in_9,
  input  in_10,
  input  in_11,
  output out_12,
  output out_13,
  output out_14,
  output out_15,
  output out_16,
  output out_17,
  output out_18,
  output out_19,
  output out_20,
  output out_21,
  output out_22,
  output out_23,
  output out_24,
  output out_25,
  output out_26,
  output out_27,
  output out_28,
  output out_29,
  output out_30,
  output out_31,
  output out_32,
  output out_33,
  output out_34,
  output out_35,
  output out_36,
  output out_37,
  output out_38,
  output out_39,
  output out_40,
  output out_41,
  output out_42,
  output out_43,
  output out_44,
  output out_45,
  output out_46,
  output out_47
);

  wire and_1_out, and_2_out, and_3_out, and_4_out, and_5_out, and_6_out, and_7_out, and_8_out, and_9_out,
       and_10_out, and_11_out, and_12_out, and_13_out, and_14_out, and_15_out, and_16_out, and_17_out,
       and_18_out, and_19_out, and_20_out, and_21_out, and_22_out, and_23_out, and_24_out, and_25_out,
       and_26_out, and_27_out, and_28_out, and_29_out, and_30_out, and_31_out, and_32_out, and_37_out,
       and_38_out, and_39_out, and_40_out, and_41_out, and_42_out, and_43_out, and_44_out, AND_LED1,
       AND_LED2, AND_LED3, AND_LED4, comparador_4bit_1_s1, comparador_4bit_1_s2, comparador_4bit_1_s3,
       COMPARATOR_LED1, COMPARATOR_LED2, COMPARATOR_LED3, not_1_out, not_2_out, not_3_out, not_4_out,
       not_5_out, not_6_out, not_7_out, not_8_out, or_1_out, or_2_out, or_3_out, or_4_out, OR_LED1, OR_LED2,
       OR_LED3, OR_LED4, resta_7segmentoss_1_d1_a, resta_7segmentoss_1_d1_b, resta_7segmentoss_1_d1_c,
       resta_7segmentoss_1_d1_d, resta_7segmentoss_1_d1_e, resta_7segmentoss_1_d1_f,
       resta_7segmentoss_1_d1_g, resta_7segmentoss_1_d2_a, resta_7segmentoss_1_d2_b,
       resta_7segmentoss_1_d2_c, resta_7segmentoss_1_d2_d, resta_7segmentoss_1_d2_e,
       resta_7segmentoss_1_d2_f, resta_7segmentoss_1_d2_g, resta_7segmentoss_1_signo_7seg_g, RESTA_SIGNO,
       restador_4bit_1_s1, restador_4bit_1_s2, restador_4bit_1_s3, restador_4bit_1_s4, Selection_A,
       Selection_B, Selection_C, Selection_D, Selection_E, Selection_F, Selection_G, suma_7segmentoss_1_d1_a,
       suma_7segmentoss_1_d1_b, suma_7segmentoss_1_d1_c, suma_7segmentoss_1_d1_d, suma_7segmentoss_1_d1_e,
       suma_7segmentoss_1_d1_f, suma_7segmentoss_1_d1_g, suma_7segmentoss_1_d2_a, suma_7segmentoss_1_d2_b,
       suma_7segmentoss_1_d2_c, suma_7segmentoss_1_d2_d, suma_7segmentoss_1_d2_e, suma_7segmentoss_1_d2_f,
       suma_7segmentoss_1_d2_g, sumador_4bit_1_s1, sumador_4bit_1_s2, sumador_4bit_1_s3, sumador_4bit_1_s4,
       sumador_4bit_1_s5, XOR_LED1, XOR_LED2, XOR_LED3, XOR_LED4;

  _7_Segment_Display u_7_segment_display_1 (
    .g(RESTA_SIGNO), .d(resta_7segmentoss_1_signo_7seg_g));  // open: f, a, b, e, c, dp
  resta_7segmentoss resta_7segmentoss_1 (
    .E1(restador_4bit_1_s1), .E2(restador_4bit_1_s2), .E3(restador_4bit_1_s3), .E4(restador_4bit_1_s4),
    .Signo(RESTA_SIGNO), .Signo_7Seg_G(resta_7segmentoss_1_signo_7seg_g), .D2_A(resta_7segmentoss_1_d2_a),
    .D2_B(resta_7segmentoss_1_d2_b), .D2_C(resta_7segmentoss_1_d2_c), .D2_D(resta_7segmentoss_1_d2_d),
    .D2_E(resta_7segmentoss_1_d2_e), .D2_F(resta_7segmentoss_1_d2_f), .D2_G(resta_7segmentoss_1_d2_g),
    .D1_A(resta_7segmentoss_1_d1_a), .D1_B(resta_7segmentoss_1_d1_b), .D1_C(resta_7segmentoss_1_d1_c),
    .D1_D(resta_7segmentoss_1_d1_d), .D1_E(resta_7segmentoss_1_d1_e), .D1_F(resta_7segmentoss_1_d1_f),
    .D1_G(resta_7segmentoss_1_d1_g));
  _7_Segment_Display u_7_segment_display_2 (
    .g(resta_7segmentoss_1_d2_g), .f(resta_7segmentoss_1_d2_f), .a(resta_7segmentoss_1_d2_a),
    .b(resta_7segmentoss_1_d2_b), .e(resta_7segmentoss_1_d2_e), .d(resta_7segmentoss_1_d2_d),
    .c(resta_7segmentoss_1_d2_c));  // open: dp
  selector selector_1 (
    .Sel2(in_9), .Sel1(in_10), .Sel0(in_11), .A(Selection_A), .B(Selection_B), .C(Selection_C),
    .D(Selection_D), .E(Selection_E), .F(Selection_F), .G(Selection_G));  // open: H
  _7_Segment_Display u_7_segment_display_3 (
    .g(resta_7segmentoss_1_d1_g), .f(resta_7segmentoss_1_d1_f), .a(resta_7segmentoss_1_d1_a),
    .b(resta_7segmentoss_1_d1_b), .e(resta_7segmentoss_1_d1_e), .d(resta_7segmentoss_1_d1_d),
    .c(resta_7segmentoss_1_d1_c));  // open: dp
  and and_1 (and_1_out, A4, Selection_A);
  and and_2 (and_2_out, A3, Selection_A);
  and and_3 (and_3_out, A2, Selection_A);
  and and_4 (and_4_out, A1, Selection_A);
  and and_5 (and_5_out, B4, Selection_A);
  and and_6 (and_6_out, B3, Selection_A);
  and and_7 (and_7_out, B2, Selection_A);
  and and_8 (and_8_out, B1, Selection_A);
  and and_9 (and_9_out, A1, Selection_B);
  and and_10 (and_10_out, A2, Selection_B);
  and and_11 (and_11_out, A3, Selection_B);
  and and_12 (and_12_out, A4, Selection_B);
  and and_13 (and_13_out, B1, Selection_B);
  and and_14 (and_14_out, B2, Selection_B);
  and and_15 (and_15_out, B3, Selection_B);
  and and_16 (and_16_out, B4, Selection_B);
  _7_Segment_Display u_7_segment_display_4 (
    .g(suma_7segmentoss_1_d2_g), .f(suma_7segmentoss_1_d2_f), .a(suma_7segmentoss_1_d2_a),
    .b(suma_7segmentoss_1_d2_b), .e(suma_7segmentoss_1_d2_e), .d(suma_7segmentoss_1_d2_d),
    .c(suma_7segmentoss_1_d2_c));  // open: dp
  suma_7segmentoss suma_7segmentoss_1 (
    .E4(sumador_4bit_1_s5), .E3(sumador_4bit_1_s4), .E2(sumador_4bit_1_s3), .E1(sumador_4bit_1_s2),
    .E0(sumador_4bit_1_s1), .D2_A(suma_7segmentoss_1_d2_a), .D2_B(suma_7segmentoss_1_d2_b),
    .D2_C(suma_7segmentoss_1_d2_c), .D2_D(suma_7segmentoss_1_d2_d), .D2_E(suma_7segmentoss_1_d2_e),
    .D2_F(suma_7segmentoss_1_d2_f), .D2_G(suma_7segmentoss_1_d2_g), .D1_A(suma_7segmentoss_1_d1_a),
    .D1_B(suma_7segmentoss_1_d1_b), .D1_C(suma_7segmentoss_1_d1_c), .D1_D(suma_7segmentoss_1_d1_d),
    .D1_E(suma_7segmentoss_1_d1_e), .D1_F(suma_7segmentoss_1_d1_f), .D1_G(suma_7segmentoss_1_d1_g));
  LED led_1 (.in(or_1_out));
  or or_1 (or_1_out, OR_LED4, AND_LED4, XOR_LED4);
  sumador_4bit sumador_4bit_1 (
    .A0(and_1_out), .A1(and_2_out), .A2(and_3_out), .A3(and_4_out), .B0(and_5_out), .B1(and_6_out),
    .B2(and_7_out), .B3(and_8_out), .S3(sumador_4bit_1_s3), .S4(sumador_4bit_1_s4), .S5(sumador_4bit_1_s5),
    .S1(sumador_4bit_1_s1), .S2(sumador_4bit_1_s2));
  _7_Segment_Display u_7_segment_display_5 (
    .g(suma_7segmentoss_1_d1_g), .f(suma_7segmentoss_1_d1_f), .a(suma_7segmentoss_1_d1_a),
    .b(suma_7segmentoss_1_d1_b), .e(suma_7segmentoss_1_d1_e), .d(suma_7segmentoss_1_d1_d),
    .c(suma_7segmentoss_1_d1_c));  // open: dp
  restador_4bit restador_4bit_1 (
    .A0(and_9_out), .A1(and_10_out), .A2(and_11_out), .A3(and_12_out), .B0(and_13_out), .B1(and_14_out),
    .B2(and_15_out), .B3(and_16_out), .Signo(RESTA_SIGNO), .S1(restador_4bit_1_s1), .S2(restador_4bit_1_s2),
    .S3(restador_4bit_1_s3), .S4(restador_4bit_1_s4));
  LED led_2 (.in(or_2_out));
  or or_2 (or_2_out, COMPARATOR_LED3, AND_LED3, OR_LED3, XOR_LED3);
  LED led_3 (.in(or_3_out));
  or or_3 (or_3_out, AND_LED2, OR_LED2, XOR_LED2, COMPARATOR_LED2);
  LED led_4 (.in(or_4_out));
  or or_4 (or_4_out, XOR_LED1, OR_LED1, AND_LED1, COMPARATOR_LED1);
  suma_7segmentoss suma_7segmentoss_2 (
    .E4(sumador_4bit_1_s1), .E3(sumador_4bit_1_s2), .E2(sumador_4bit_1_s3), .E1(sumador_4bit_1_s4),
    .E0(sumador_4bit_1_s5), .D2_A(out_12), .D2_B(out_13), .D2_C(out_14), .D2_D(out_15), .D2_E(out_16),
    .D2_F(out_17), .D2_G(out_18), .D1_A(out_19), .D1_B(out_20), .D1_C(out_21), .D1_D(out_22), .D1_E(out_23),
    .D1_F(out_24), .D1_G(out_25));
  resta_7segmentoss resta_7segmentoss_2 (
    .E1(restador_4bit_1_s1), .E2(restador_4bit_1_s2), .E3(restador_4bit_1_s3), .E4(restador_4bit_1_s4),
    .Signo(RESTA_SIGNO), .Signo_7Seg_G(out_26), .D2_A(out_27), .D2_B(out_28), .D2_C(out_29), .D2_D(out_30),
    .D2_E(out_31), .D2_F(out_32), .D2_G(out_33), .D1_A(out_34), .D1_B(out_35), .D1_C(out_36), .D1_D(out_37),
    .D1_E(out_38), .D1_F(out_39));  // open: D1_G
  and and_17 (and_17_out, B4, Selection_C);
  and and_18 (and_18_out, B3, Selection_C);
  and and_19 (and_19_out, B2, Selection_C);
  and and_20 (and_20_out, B1, Selection_C);
  and and_21 (and_21_out, A1, Selection_C);
  and and_22 (and_22_out, A2, Selection_C);
  and and_23 (and_23_out, A3, Selection_C);
  and and_24 (and_24_out, A4, Selection_C);
  and and_25 (and_25_out, B4, Selection_E);
  and and_26 (and_26_out, B3, Selection_E);
  and and_27 (and_27_out, B2, Selection_E);
  and and_28 (and_28_out, B1, Selection_E);
  and and_29 (and_29_out, A1, Selection_E);
  and and_30 (and_30_out, A2, Selection_E);
  and and_31 (and_31_out, A3, Selection_E);
  and and_32 (and_32_out, A4, Selection_E);
  and and_33 (AND_LED4, and_20_out, and_21_out);
  and and_34 (AND_LED3, and_19_out, and_22_out);
  xor xor_1 (XOR_LED4, and_28_out, and_29_out);
  xor xor_2 (XOR_LED3, and_27_out, and_30_out);
  and and_35 (AND_LED2, and_18_out, and_23_out);
  and and_36 (AND_LED1, and_17_out, and_24_out);
  xor xor_3 (XOR_LED2, and_26_out, and_31_out);
  xor xor_4 (XOR_LED1, and_25_out, and_32_out);
  and and_37 (and_37_out, B4, Selection_D);
  and and_38 (and_38_out, B3, Selection_D);
  and and_39 (and_39_out, B2, Selection_D);
  and and_40 (and_40_out, B1, Selection_D);
  and and_41 (and_41_out, A1, Selection_D);
  and and_42 (and_42_out, A2, Selection_D);
  and and_43 (and_43_out, A3, Selection_D);
  and and_44 (and_44_out, A4, Selection_D);
  or or_5 (OR_LED4, and_40_out, and_41_out);
  or or_6 (OR_LED3, and_39_out, and_42_out);
  or or_7 (OR_LED2, and_38_out, and_43_out);
  comparador_4bit comparador_4bit_1 (
    .A3(A1), .A2(A2), .A1(A3), .A0(A4), .B3(B1), .B2(B2), .B1(B3), .B0(B4), .S1(comparador_4bit_1_s1),
    .S2(comparador_4bit_1_s2), .S3(comparador_4bit_1_s3));
  or or_8 (OR_LED1, and_37_out, and_44_out);
  and and_45 (COMPARATOR_LED3, comparador_4bit_1_s1, Selection_F);
  and and_46 (COMPARATOR_LED2, comparador_4bit_1_s2, Selection_F);
  and and_47 (COMPARATOR_LED1, comparador_4bit_1_s3, Selection_F);
  not not_1 (not_1_out, A1);
  not not_2 (not_2_out, A2);
  not not_3 (not_3_out, A3);
  not not_4 (not_4_out, A4);
  not not_5 (not_5_out, B1);
  not not_6 (not_6_out, B2);
  not not_7 (not_7_out, B3);
  not not_8 (not_8_out, B4);
  and and_48 (out_40, Selection_G, not_1_out);
  and and_49 (out_41, Selection_G, not_2_out);
  and and_50 (out_42, Selection_G, not_3_out);
  and and_51 (out_43, Selection_G, not_4_out);
  and and_52 (out_44, Selection_G, not_5_out);
  and and_53 (out_45, Selection_G, not_6_out);
  and and_54 (out_46, Selection_G, not_7_out);
  and and_55 (out_47, Selection_G, not_8_out);

  // Other names for the same wires on the sheet: NA1 = out_40; NA2 = out_41; NA3 = out_42; NA4 = out_43; NB1 = out_44;
  //   NB2 = out_45; NB3 = out_46; NB4 = out_47

  // Notes on the sheet:
  //   Resta Display 7Seg
  //   Decision en binario (ABC)
  //   000 = suma
  //   001 = resta
  //   010 = AND
  //   011 = OR
  //   100 = XOR
  //   101 = Comparador
  //   110 = not
  //   Circuito de Suma
  //   Suma Display 7Seg
  //   A and B
  //   A xor B
  //   A or B
  //   Cuando la seleccion sea COMPARADOR (101)
  //   3 LEDS ENCENDIDOS -> A = B
  //   2 LEDS ENCENDIDOS -> A > B
  //   1 LED ENCENDIDO -> A < B
  //   not ENTRADA_A  
  //   not ENTRADA_B
  //   ENTRADA_A and ENTRADA_B
  //   ENTRADA_A xor ENTRADA_B
  //   COMPARADOR
  //   ENTRADA_A & ENTRADA_B
  //   ENTRADA_A or ENTRADA_B
  //   not ENTRADA_A  
  //   not ENTRADA_B
endmodule

module sumador_4bit (
  input  A0,
  input  A1,
  input  A2,
  input  A3,
  input  B0,
  input  B1,
  input  B2,
  input  B3,
  output S1,
  output S2,
  output S3,
  output S4,
  output S5
);

  wire sumador_completo_1_carry_out, sumador_completo_2_carry_out, sumador_completo_3_carry_out;

  sumador_completo sumador_completo_1 (
    .A(A0), .B(B0), .Carry_in(1'b0), .Salida(S1), .Carry_out(sumador_completo_1_carry_out));
  sumador_completo sumador_completo_2 (
    .A(A1), .B(B1), .Carry_in(sumador_completo_1_carry_out), .Salida(S2),
    .Carry_out(sumador_completo_2_carry_out));
  sumador_completo sumador_completo_3 (
    .A(A2), .B(B2), .Carry_in(sumador_completo_2_carry_out), .Salida(S3),
    .Carry_out(sumador_completo_3_carry_out));
  sumador_completo sumador_completo_4 (
    .A(A3), .B(B3), .Carry_in(sumador_completo_3_carry_out), .Salida(S4), .Carry_out(S5));

  // Notes on the sheet:
  //   Entrada A
  //   Entrada B
endmodule

module sumador_completo (
  input  A,
  input  B,
  input  Carry_in,
  output Salida,
  output Carry_out
);

  wire and_1_out, and_2_out, xor_1_out;

  xor xor_1 (xor_1_out, A, B);
  and and_1 (and_1_out, xor_1_out, Carry_in);
  and and_2 (and_2_out, B, A);
  xor xor_2 (Salida, xor_1_out, Carry_in);
  or or_1 (Carry_out, and_1_out, and_2_out);
endmodule

module restador_4bit (
  input  A0,
  input  A1,
  input  A2,
  input  A3,
  input  B0,
  input  B1,
  input  B2,
  input  B3,
  output Signo,
  output S1,
  output S2,
  output S3,
  output S4
);

  wire and_1_out, and_2_out, and_3_out, and_4_out, and_5_out, and_6_out, and_7_out, and_8_out, CS1, CS2, CS3,
       CS4, not_1_out, not_2_out, not_3_out, not_4_out, not_5_out, restador_completo_1_carry_out,
       restador_completo_2_carry_out, restador_completo_3_carry_out, S1_t, S2_t, S3_t, S4_t,
       sumador_4bit_1_s5;

  not not_1 (not_1_out, S1_t);
  not not_2 (not_2_out, S2_t);
  not not_3 (not_3_out, S3_t);
  not not_4 (not_4_out, S4_t);
  restador_completo restador_completo_1 (
    .A(A0), .B(B0), .Carry_in(1'b1), .Salida(S1_t), .Carry_out(restador_completo_1_carry_out));
  sumador_4bit sumador_4bit_1 (
    .A0(not_1_out), .A1(not_2_out), .A2(not_3_out), .A3(not_4_out), .B0(1'b1), .B1(1'b0), .B2(1'b0),
    .B3(1'b0), .S3(CS3), .S4(CS4), .S5(sumador_4bit_1_s5), .S1(CS1), .S2(CS2));
  restador_completo restador_completo_2 (
    .A(A1), .B(B1), .Carry_in(restador_completo_1_carry_out), .Salida(S2_t),
    .Carry_out(restador_completo_2_carry_out));
  not not_5 (not_5_out, Signo);
  restador_completo restador_completo_3 (
    .A(A2), .B(B2), .Carry_in(restador_completo_2_carry_out), .Salida(S3_t),
    .Carry_out(restador_completo_3_carry_out));
  and and_1 (and_1_out, S1_t, Signo);
  and and_2 (and_2_out, S2_t, Signo);
  and and_3 (and_3_out, S3_t, Signo);
  and and_4 (and_4_out, S4_t, Signo);
  and and_5 (and_5_out, CS1, not_5_out);
  and and_6 (and_6_out, CS2, not_5_out);
  and and_7 (and_7_out, CS3, not_5_out);
  and and_8 (and_8_out, CS4, not_5_out);
  or or_1 (S1, and_1_out, and_5_out);
  or or_2 (S2, and_2_out, and_6_out);
  or or_3 (S3, and_3_out, and_7_out);
  or or_4 (S4, and_4_out, and_8_out);
  restador_completo restador_completo_4 (
    .A(A3), .B(B3), .Carry_in(restador_completo_3_carry_out), .Salida(S4_t), .Carry_out(Signo));

  // Other names for the same wires on the sheet: S5 = Signo

  // Notes on the sheet:
  //   Entrada A
  //   Entrada B
  //   complemento a1
  //   complemento a2
  //   si el numero es negativo
endmodule

module restador_completo (
  input  A,
  input  B,
  input  Carry_in,
  output Salida,
  output Carry_out
);

  wire and_1_out, and_2_out, not_1_out, xor_1_out;

  not not_1 (not_1_out, B);
  xor xor_1 (xor_1_out, A, not_1_out);
  and and_1 (and_1_out, xor_1_out, Carry_in);
  and and_2 (and_2_out, not_1_out, A);
  xor xor_2 (Salida, xor_1_out, Carry_in);
  or or_1 (Carry_out, and_1_out, and_2_out);
endmodule

module comparador_4bit (
  input  A3,
  input  A2,
  input  A1,
  input  A0,
  input  B3,
  input  B2,
  input  B1,
  input  B0,
  output S1,
  output S2,
  output S3
);

  wire comparador_1_s1, comparador_1_s2, comparador_1_s3;

  comparador comparador_1 (
    .A3(A3), .A2(A2), .A1(A1), .A0(A0), .B3(B3), .B2(B2), .B1(B1), .B0(B0), .S1(comparador_1_s1),
    .S2(comparador_1_s2), .S3(comparador_1_s3));
  led_comparador led_comparador_1 (
    .E1(comparador_1_s1), .E2(comparador_1_s2), .E3(comparador_1_s3), .S1(S1), .S2(S2), .S3(S3));
endmodule

module comparador (
  input  A3,
  input  A2,
  input  A1,
  input  A0,
  input  B3,
  input  B2,
  input  B1,
  input  B0,
  output S1,
  output S2,
  output S3
);

  wire and_1_out, and_2_out, and_3_out, and_4_out, and_5_out, and_6_out, and_7_out, and_8_out, and_9_out,
       and_10_out, and_11_out, and_12_out, and_13_out, and_14_out, and_15_out, and_16_out, and_17_out,
       and_18_out, and_19_out, and_20_out, and_21_out, and_22_out, and_23_out, and_24_out, and_25_out,
       and_26_out, and_27_out, and_28_out, and_29_out, and_30_out, and_31_out, and_32_out, and_33_out,
       and_34_out, and_35_out, and_36_out, and_37_out, and_38_out, and_39_out, and_40_out, and_41_out,
       and_42_out, and_43_out, and_44_out, and_45_out, and_46_out, not_1_out, not_2_out, not_3_out,
       not_4_out, not_5_out, not_6_out, not_7_out, not_8_out;

  not not_1 (not_1_out, A3);
  not not_2 (not_2_out, A2);
  not not_3 (not_3_out, A1);
  not not_4 (not_4_out, A0);
  not not_5 (not_5_out, B3);
  not not_6 (not_6_out, B2);
  not not_7 (not_7_out, B1);
  not not_8 (not_8_out, B0);
  and and_1 (and_1_out, not_1_out, not_2_out, not_3_out, not_4_out, not_5_out, not_6_out, not_7_out, not_8_out);
  and and_2 (and_2_out, not_1_out, not_2_out, A1, not_4_out, not_5_out, not_6_out, B1, not_8_out);
  and and_3 (and_3_out, not_1_out, A2, not_3_out, not_4_out, not_5_out, B2, not_7_out, not_8_out);
  and and_4 (and_4_out, not_1_out, A2, A1, not_4_out, not_5_out, B2, B1, not_8_out);
  and and_5 (and_5_out, A3, not_2_out, not_3_out, not_4_out, B3, not_6_out, not_7_out, not_8_out);
  and and_6 (and_6_out, A3, not_2_out, A1, not_4_out, B3, not_6_out, B1, not_8_out);
  and and_7 (and_7_out, A3, A2, not_3_out, not_4_out, B3, B2, not_7_out, not_8_out);
  and and_8 (and_8_out, A3, A2, A1, not_4_out, B3, B2, B1, not_8_out);
  and and_9 (and_9_out, not_1_out, not_2_out, not_3_out, A0, not_5_out, not_6_out, not_7_out, B0);
  and and_10 (and_10_out, not_1_out, not_2_out, A1, A0, not_5_out, not_6_out, B1, B0);
  and and_11 (and_11_out, not_1_out, A2, not_3_out, A0, not_5_out, B2, not_7_out, B0);
  and and_12 (and_12_out, not_1_out, A2, A1, A0, not_5_out, B2, B1, B0);
  and and_13 (and_13_out, A3, not_2_out, not_3_out, A0, B3, not_6_out, not_7_out, B0);
  and and_14 (and_14_out, A3, not_2_out, A1, A0, B3, not_6_out, B1, B0);
  and and_15 (and_15_out, A3, A2, not_3_out, A0, B3, B2, not_7_out, B0);
  and and_16 (and_16_out, A3, A2, A1, A0, B3, B2, B1, B0);
  and and_17 (and_17_out, A0, not_5_out, not_6_out, not_7_out, not_8_out);
  and and_18 (and_18_out, A1, not_5_out, not_6_out, not_7_out);
  and and_19 (and_19_out, A1, A0, not_5_out, not_6_out, not_8_out);
  and and_20 (and_20_out, A2, not_5_out, not_6_out);
  and and_21 (and_21_out, A2, A0, not_5_out, not_7_out, not_8_out);
  and and_22 (and_22_out, A2, A1, not_5_out, not_7_out);
  and and_23 (and_23_out, A2, A1, A0, not_5_out, not_8_out);
  and and_24 (and_24_out, A3, not_5_out);
  and and_25 (and_25_out, A3, A0, not_6_out, not_7_out, not_8_out);
  and and_26 (and_26_out, A3, A1, not_6_out, not_7_out);
  and and_27 (and_27_out, A3, A1, A0, not_6_out, not_8_out);
  and and_28 (and_28_out, A3, A2, not_6_out);
  and and_29 (and_29_out, A3, A2, A0, not_7_out, not_8_out);
  and and_30 (and_30_out, A3, A2, A1, not_7_out);
  and and_31 (and_31_out, A3, A2, A1, A0, not_8_out);
  and and_32 (and_32_out, not_1_out, not_2_out, not_3_out, not_4_out, B0);
  and and_33 (and_33_out, not_1_out, not_2_out, not_3_out, B1);
  and and_34 (and_34_out, not_1_out, not_2_out, B2);
  and and_35 (and_35_out, not_1_out, B3);
  and and_36 (and_36_out, not_1_out, not_2_out, not_4_out, B1, B0);
  and and_37 (and_37_out, not_1_out, not_3_out, not_4_out, B2, B0);
  and and_38 (and_38_out, not_1_out, not_3_out, B2, B1);
  and and_39 (and_39_out, not_1_out, not_4_out, B2, B1, B0);
  and and_40 (and_40_out, not_2_out, not_3_out, not_4_out, B3, B0);
  and and_41 (and_41_out, not_2_out, not_3_out, B3, B1);
  and and_42 (and_42_out, not_2_out, B3, B2);
  and and_43 (and_43_out, not_2_out, not_4_out, B3, B1, B0);
  and and_44 (and_44_out, not_3_out, not_4_out, B3, B2, B0);
  and and_45 (and_45_out, not_3_out, B3, B2, B1);
  and and_46 (and_46_out, not_4_out, B3, B2, B1, B0);
  or or_1 (S1, and_1_out, and_2_out, and_3_out, and_4_out, and_5_out, and_6_out, and_7_out, and_8_out, and_9_out, and_10_out, and_11_out, and_12_out, and_13_out, and_14_out, and_15_out, and_16_out);
  or or_2 (S2, and_17_out, and_18_out, and_19_out, and_20_out, and_21_out, and_22_out, and_23_out, and_24_out, and_25_out, and_26_out, and_27_out, and_28_out, and_29_out, and_30_out, and_31_out);
  or or_3 (S3, and_32_out, and_33_out, and_34_out, and_35_out, and_36_out, and_37_out, and_38_out, and_39_out, and_40_out, and_41_out, and_42_out, and_43_out, and_44_out, and_45_out, and_46_out);
endmodule

module led_comparador (
  input  E1,
  input  E2,
  input  E3,
  output S1,
  output S2,
  output S3
);

  wire and_2_out, and_3_out, and_4_out, and_5_out, and_6_out, not_1_out, not_2_out, not_3_out;

  not not_1 (not_1_out, E1);
  not not_2 (not_2_out, E2);
  not not_3 (not_3_out, E3);
  and and_1 (S1, E1, not_2_out, not_3_out);
  and and_2 (and_2_out, not_1_out, E2, not_3_out);
  and and_3 (and_3_out, E1, not_2_out, not_3_out);
  and and_4 (and_4_out, not_1_out, not_2_out, E3);
  and and_5 (and_5_out, not_1_out, E2, not_3_out);
  and and_6 (and_6_out, E1, not_2_out, not_3_out);
  or or_1 (S2, and_2_out, and_3_out);
  or or_2 (S3, and_4_out, and_5_out, and_6_out);
endmodule

module selector (
  input  Sel2,
  input  Sel1,
  input  Sel0,
  output A,
  output B,
  output C,
  output D,
  output E,
  output F,
  output G,
  output H
);

  wire not_1_out, not_2_out, not_3_out, not_4_out;

  not not_1 (not_1_out, Sel2);
  not not_2 (not_2_out, Sel1);
  not not_3 (not_3_out, Sel0);
  not not_4 (not_4_out, Sel0);
  and and_1 (A, not_1_out, not_2_out, not_3_out);
  and and_2 (B, not_1_out, not_2_out, Sel0);
  and and_3 (C, not_1_out, Sel1, not_3_out);
  and and_4 (D, not_1_out, Sel1, Sel0);
  and and_5 (E, Sel2, not_2_out, not_3_out);
  and and_6 (F, Sel2, not_2_out, Sel0);
  and and_7 (G, Sel2, Sel1);
endmodule

module suma_7segmentoss (
  input  E4,
  input  E3,
  input  E2,
  input  E1,
  input  E0,
  output D2_A,
  output D2_B,
  output D2_C,
  output D2_D,
  output D2_E,
  output D2_F,
  output D2_G,
  output D1_A,
  output D1_B,
  output D1_C,
  output D1_D,
  output D1_E,
  output D1_F,
  output D1_G
);

  wire and_1_out, and_2_out, and_3_out, and_4_out, and_5_out, and_6_out, and_7_out, and_8_out, and_9_out,
       and_10_out, and_11_out, and_12_out, and_13_out, and_14_out, and_15_out, and_16_out, and_17_out,
       and_18_out, and_19_out, and_20_out, and_21_out, and_22_out, and_23_out, and_24_out, and_25_out,
       and_26_out, and_27_out, and_28_out, and_29_out, and_30_out, and_31_out, and_32_out, and_33_out,
       and_34_out, and_35_out, and_36_out, and_37_out, and_38_out, and_39_out, and_40_out, and_41_out,
       and_42_out, and_43_out, and_44_out, and_45_out, and_46_out, and_47_out, and_48_out, and_49_out,
       and_50_out, and_51_out, and_52_out, and_53_out, and_54_out, and_55_out, and_56_out, and_57_out,
       and_58_out, and_59_out, and_60_out, and_61_out, and_62_out, and_63_out, and_64_out, and_65_out,
       and_66_out, and_67_out, and_68_out, and_69_out, and_70_out, and_71_out, not_1_out, not_2_out,
       not_3_out, not_4_out, not_5_out;

  not not_1 (not_1_out, E4);
  not not_2 (not_2_out, E3);
  not not_3 (not_3_out, E2);
  not not_4 (not_4_out, E1);
  not not_5 (not_5_out, E0);
  and and_1 (and_1_out, not_1_out, not_2_out);
  and and_2 (and_2_out, E4, E3);
  and and_3 (and_3_out, not_1_out, not_3_out, not_4_out);
  and and_4 (and_4_out, E4, E2);
  and and_5 (and_5_out, not_2_out, not_3_out);
  and and_6 (and_6_out, E3, E2, E1);
  and and_7 (and_7_out, not_1_out, not_2_out);
  and and_8 (and_8_out, E4, E3);
  and and_9 (and_9_out, not_1_out, not_3_out, not_4_out);
  and and_10 (and_10_out, E4, E2);
  and and_11 (and_11_out, not_1_out, not_2_out);
  and and_12 (and_12_out, not_2_out, E2);
  and and_13 (and_13_out, E4, E3, not_3_out);
  and and_14 (and_14_out, not_1_out, not_3_out, not_4_out);
  and and_15 (and_15_out, E4, E2, not_4_out);
  and and_16 (and_16_out, not_1_out, not_2_out);
  and and_17 (and_17_out, not_1_out, not_3_out, not_4_out);
  and and_18 (and_18_out, E4, E2);
  and and_19 (and_19_out, E4, E3);
  and and_20 (and_20_out, not_2_out, E1);
  and and_21 (and_21_out, not_1_out, E2, E0);
  and and_22 (and_22_out, E4, not_2_out, not_5_out);
  and and_23 (and_23_out, not_1_out, not_3_out, not_5_out);
  and and_24 (and_24_out, E4, not_3_out, E0);
  and and_25 (and_25_out, E3, not_4_out, E0);
  and and_26 (and_26_out, E3, E2, not_4_out);
  and and_27 (and_27_out, E4, E1, not_5_out);
  and and_28 (and_28_out, not_2_out, E1, E0);
  and and_29 (and_29_out, E3, not_4_out, not_5_out);
  and and_30 (and_30_out, E4, not_2_out, E0);
  and and_31 (and_31_out, E4, not_2_out, E1);
  and and_32 (and_32_out, not_1_out, not_3_out);
  and and_33 (and_33_out, E2, not_4_out, not_5_out);
  and and_34 (and_34_out, E3, E2, not_4_out);
  and and_35 (and_35_out, E3, E2, not_5_out);
  and and_36 (and_36_out, E4, E1, E0);
  and and_37 (and_37_out, E4, not_3_out);
  and and_38 (and_38_out, not_1_out, not_2_out, E2);
  and and_39 (and_39_out, not_3_out, not_4_out);
  and and_40 (and_40_out, E4, not_4_out);
  and and_41 (and_41_out, E3, E1);
  and and_42 (and_42_out, not_2_out, not_3_out, E1);
  and and_43 (and_43_out, not_1_out, E2, not_4_out, E0);
  and and_44 (and_44_out, not_2_out, E1, not_5_out);
  and and_45 (and_45_out, not_1_out, E3, E2, E0);
  and and_46 (and_46_out, E4, not_2_out, E1);
  and and_47 (and_47_out, E3, not_4_out, E0);
  and and_48 (and_48_out, E4, not_2_out, not_5_out);
  and and_49 (and_49_out, not_1_out, not_3_out, not_5_out);
  and and_50 (and_50_out, E3, E2, not_4_out);
  and and_51 (and_51_out, E4, E1, not_5_out);
  and and_52 (and_52_out, not_2_out, E1, not_5_out);
  and and_53 (and_53_out, E4, not_2_out, not_5_out);
  and and_54 (and_54_out, not_1_out, not_3_out, not_5_out);
  and and_55 (and_55_out, E3, E2, not_4_out, not_5_out);
  and and_56 (and_56_out, E4, E1, not_5_out);
  and and_57 (and_57_out, not_1_out, not_2_out, E2, not_4_out);
  and and_58 (and_58_out, E3, not_3_out, not_4_out);
  and and_59 (and_59_out, not_1_out, E3, E2, E1);
  and and_60 (and_60_out, E4, not_2_out, not_3_out, E1);
  and and_61 (and_61_out, E4, E3, not_4_out);
  and and_62 (and_62_out, not_2_out, not_4_out, not_5_out);
  and and_63 (and_63_out, E3, E1, not_5_out);
  and and_64 (and_64_out, not_1_out, not_2_out, E2, not_5_out);
  and and_65 (and_65_out, not_2_out, not_3_out, E1);
  and and_66 (and_66_out, not_1_out, E2, not_4_out);
  and and_67 (and_67_out, E3, not_4_out);
  and and_68 (and_68_out, not_1_out, E3, E2);
  and and_69 (and_69_out, E4, not_3_out, not_5_out);
  and and_70 (and_70_out, E4, not_2_out, E1);
  and and_71 (and_71_out, not_2_out, E1, not_5_out);
  or or_1 (D2_A, and_1_out, and_2_out, and_3_out, and_4_out);
  or or_2 (D2_C, not_1_out, and_5_out, and_6_out);
  or or_3 (D2_D, and_7_out, and_8_out, and_9_out, and_10_out);
  or or_4 (D2_E, and_11_out, and_12_out, and_13_out, and_14_out, and_15_out);
  or or_5 (D2_F, and_16_out, and_17_out);
  or or_6 (D2_G, and_18_out, and_19_out);
  or or_7 (D1_A, and_20_out, and_21_out, and_22_out, and_23_out, and_24_out, and_25_out, and_26_out, and_27_out);
  or or_8 (D1_B, and_28_out, and_29_out, and_30_out, and_31_out, and_32_out, and_33_out, and_34_out, and_35_out, and_36_out);
  or or_9 (D1_C, E0, and_37_out, and_38_out, and_39_out, and_40_out, and_41_out);
  or or_10 (D1_E, and_52_out, and_53_out, and_54_out, and_55_out, and_56_out);
  or or_11 (D1_F, and_57_out, and_58_out, and_59_out, and_60_out, and_61_out, and_62_out, and_63_out, and_64_out);
  or or_12 (D1_G, and_65_out, and_66_out, and_67_out, and_68_out, and_69_out, and_70_out, and_71_out);
  or or_13 (D1_D, and_42_out, and_43_out, and_44_out, and_45_out, and_46_out, and_47_out, and_48_out, and_49_out, and_50_out, and_51_out);

  assign D2_B = 1'b1;
endmodule

module resta_7segmentoss (
  input  E1,
  input  E2,
  input  E3,
  input  E4,
  input  Signo,
  output Signo_7Seg_G,
  output D2_A,
  output D2_B,
  output D2_C,
  output D2_D,
  output D2_E,
  output D2_F,
  output D2_G,
  output D1_A,
  output D1_B,
  output D1_C,
  output D1_D,
  output D1_E,
  output D1_F,
  output D1_G
);

  wire and_1_out, and_2_out, and_3_out, and_4_out, and_5_out, and_6_out, and_7_out, and_8_out, and_9_out,
       and_10_out, and_11_out, and_12_out, and_13_out, and_14_out, and_15_out, and_16_out, and_17_out,
       and_18_out, and_19_out, and_20_out, and_21_out, and_22_out, and_23_out, and_24_out, and_25_out,
       and_26_out, and_27_out, and_28_out, and_29_out, and_30_out, and_31_out, and_32_out, and_33_out,
       and_34_out, and_35_out, not_1_out, not_2_out, not_3_out, not_4_out;

  not not_1 (not_1_out, E1);
  not not_2 (not_2_out, E2);
  not not_3 (not_3_out, E3);
  not not_4 (not_4_out, E4);
  not not_5 (Signo_7Seg_G, Signo);
  or or_1 (D2_A, not_1_out, and_1_out);
  and and_1 (and_1_out, not_2_out, not_3_out);
  or or_2 (D2_D, not_1_out, and_2_out);
  and and_2 (and_2_out, not_2_out, not_3_out);
  or or_3 (D2_E, not_1_out, and_3_out);
  and and_3 (and_3_out, not_2_out, not_3_out);
  or or_4 (D2_F, not_1_out, and_4_out);
  and and_4 (and_4_out, not_2_out, not_3_out);
  and and_5 (and_5_out, not_2_out, not_4_out);
  and and_6 (and_6_out, not_1_out, E3);
  and and_7 (and_7_out, E2, E4);
  and and_8 (and_8_out, E1, not_3_out);
  and and_9 (and_9_out, not_3_out, not_4_out);
  and and_10 (and_10_out, not_1_out, E3, E4);
  and and_11 (and_11_out, E1, not_3_out);
  and and_12 (and_12_out, E1, not_4_out);
  and and_13 (and_13_out, not_2_out, not_3_out);
  and and_14 (and_14_out, not_1_out, E2);
  and and_15 (and_15_out, E1, E3);
  and and_16 (and_16_out, not_2_out, not_4_out);
  and and_17 (and_17_out, not_1_out, not_2_out, E3);
  and and_18 (and_18_out, E2, not_3_out, E4);
  and and_19 (and_19_out, not_1_out, E3, not_4_out);
  and and_20 (and_20_out, E1, not_3_out);
  and and_21 (and_21_out, E1, E2, E4);
  and and_22 (and_22_out, not_2_out, not_4_out);
  and and_23 (and_23_out, E1, not_3_out, not_4_out);
  or or_5 (D1_E, and_22_out, and_23_out, and_24_out);
  and and_24 (and_24_out, not_1_out, E3, not_4_out);
  and and_25 (and_25_out, not_1_out, E2, not_3_out);
  and and_26 (and_26_out, E1, not_2_out, not_3_out);
  and and_27 (and_27_out, E1, E2, E3);
  and and_28 (and_28_out, E1, not_2_out, not_4_out);
  and and_29 (and_29_out, not_1_out, not_3_out, not_4_out);
  and and_30 (and_30_out, E2, E3, not_4_out);
  and and_31 (and_31_out, not_1_out, not_2_out, E3);
  and and_32 (and_32_out, E2, not_3_out);
  and and_33 (and_33_out, E1, not_3_out);
  and and_34 (and_34_out, E1, E2);
  and and_35 (and_35_out, E2, not_4_out);
  or or_6 (D1_A, and_5_out, and_6_out, and_7_out, and_8_out);
  or or_7 (D1_B, not_2_out, and_9_out, and_10_out, and_11_out, and_12_out);
  or or_8 (D1_C, E4, and_13_out, and_14_out, and_15_out);
  or or_9 (D1_D, and_16_out, and_17_out, and_18_out, and_19_out, and_20_out, and_21_out);
  or or_10 (D1_F, and_25_out, and_26_out, and_27_out, and_28_out, and_29_out, and_30_out);
  or or_11 (D1_G, and_31_out, and_32_out, and_33_out, and_34_out, and_35_out);

  assign D2_B = 1'b1;
  assign D2_C = 1'b1;
  assign D2_G = 1'b0;
endmodule
